# Fritzing sketch rangkaiansistem (saved by Fritzing 0.9.3b)
breadboards: 1

parts:
  R1 = Photocell (LDR) [package=THT]
  YL-83_-_Control_Board2 = richardbruneau00000
  YL-83_-_Detection_Board1 = YL-83 Rain Sensor - Detection Board
  U1 = NodeMCU V1.0
  J1 = Basic Servo
  R2 = Resistor [tolerance=±5% resistance=220 package="0603 [SMD]"]
  DHT11_1 = DHT11 module

nets:
  N1: R1.pin_0, YL-83_-_Control_Board2.connector8, U1.Vin
  N2: R1.pin_1, YL-83_-_Control_Board2.connector11, U1.A0, R2.Pin_0
  GND: YL-83_-_Control_Board2.connector9, U1.GND, J1.gnd, R2.Pin_1, DHT11_1.GND
  N3: YL-83_-_Control_Board2.connector12, YL-83_-_Detection_Board1.POS
  N4: YL-83_-_Control_Board2.connector13, YL-83_-_Detection_Board1.NEG
  VCC: U1.3V3, J1.vcc, DHT11_1.VCC
  N5: U1.D5, J1.pulse, DHT11_1.DATA

custom parts:
  YL-83 Rain Sensor - Detection Board: The YL-83 is a rain sensor that has more resistance when dry and less resistance when wet. The module runs at 5V.
  NodeMCU V1.0: ESP8266 based NodeMCU
  DHT11 module: DHT11 black pcb module
